# Fritzing sketch RelesWemos_TelegramBot_ESP8266 (saved by Fritzing 0.9.6b)
breadboards: 1

parts:
  WeMos_D1_Mini1 = WeMos D1 Mini
  LED1 = RGB LED (com. cathode, rgb) [package="5 mm [THT]"]
  Mod1 = KY-019 5V Relay Module [package="Breakout board"]
  Mod2 = KY-019 5V Relay Module [package="Breakout board"]
  Mod3 = KY-019 5V Relay Module [package="Breakout board"]
  Mod4 = KY-019 5V Relay Module [package="Breakout board"]
  R1 = Resistor [tolerance=±5% power=0.25 resistance=220 package=THT]
  S1 = Pushbutton [package="[THT]"]
  R2 = Resistor [tolerance=±5% power=0.25 resistance=220 package=THT]

nets:
  N1: WeMos_D1_Mini1.5V, WeMos_D1_Mini1.G, Mod1.+, Mod1.-, Mod2.+, Mod2.-, Mod3.+, Mod3.-, Mod4.+, Mod4.-, R1.Pin_1, S1.Pin_1, S1.Pin_2, R2.Pin_1
  N2: WeMos_D1_Mini1.D1, Mod1.S
  N3: WeMos_D1_Mini1.D2, Mod2.S
  N4: WeMos_D1_Mini1.D3, Mod3.S
  N5: WeMos_D1_Mini1.D4, Mod4.S
  N6: WeMos_D1_Mini1.D5, LED1.red_anode
  N7: WeMos_D1_Mini1.D6, LED1.green_anode
  N8: WeMos_D1_Mini1.D7, LED1.blue_anode
  N9: WeMos_D1_Mini1.D8, S1.Pin_3, S1.Pin_4, R2.Pin_0
  N10: LED1.common_cathode, R1.Pin_0

custom parts:
  KY-019 5V Relay Module: KY-019 5V Relay module, used to control AC circuits. (Special thanks to vanepp for fixing the PCB holes and other errors)
